# Fritzing sketch cameraproject (saved by Fritzing 0.4.3b)
breadboards: 1

parts:
  Dwengo_Board1 = Dwengo Board
  Q1 = NPN-Transistor [package="TO92 [THT]"]
  R1 = Resistor [resistance=1M package=THT]
  VCC1 = Battery block 9V
  R2 = Resistor [resistance=2.2k package=THT]
  IC1 = SIP - 2 pins [chip_label=CAMERA spacing=300mil package="SIP (Single Inline) [THT]"]

nets:
  N1: Dwengo_Board1.connector12, Q1.C, VCC1.-
  N2: Dwengo_Board1.connector35, R2.Pin_1
  N3: Q1.E, R1.Pin_1, IC1.pin1
  N4: Q1.B, R2.Pin_0
  N5: R1.Pin_0, VCC1.+
